// Logisim project 24_bit_cpu.circ as structural Verilog: 14 circuits, main circuit Main
module Main (
);

  wire cpu_24bit_1_cpu_clock, cpu_24bit_1_load_ram_address, cpu_24bit_1_ram_output_enabled,
       cpu_24bit_1_ram_read, cpu_24bit_1_ram_write, Dec_Hex_sw1, Reset_RAM_out, Reset_System_out;
  wire [1:0] cpu_24bit_1_ep0, cpu_24bit_1_ep1, or_1_out;
  wire [3:0] valuedisplay_1_o1, valuedisplay_1_o2, valuedisplay_1_o3, valuedisplay_1_o4, valuedisplay_1_o5,
       valuedisplay_1_o6, valuedisplay_1_o7, valuedisplay_1_o8;
  wire [7:0] joystick_1_x;
  wire [23:0] cpu_24bit_1_cpu_bus_output, register_24bit_1_output_display;

  Button Reset_System (.out(Reset_System_out));
  Button Reset_RAM (.out(Reset_RAM_out));
  CPU_24Bit cpu_24bit_1 (
    .Reset_System(Reset_System_out), .CPU_Bus_Input(cpu_24bit_1_cpu_bus_output), .EP0(cpu_24bit_1_ep0),
    .EP1(cpu_24bit_1_ep1), .CPU_Bus_Output(cpu_24bit_1_cpu_bus_output),
    .Load_RAM_Address(cpu_24bit_1_load_ram_address), .RAM_Read(cpu_24bit_1_ram_read),
    .RAM_Write(cpu_24bit_1_ram_write), .RAM_Output_Enabled(cpu_24bit_1_ram_output_enabled),
    .CPU_Clock(cpu_24bit_1_cpu_clock));  // open: EP4, EP5, EP6, EP7, EP8, EP9, EPA, EPB, EPC, EPD, EPE, EPF, EP2, EP3, Raw_CPU_Clock
  RAM_Chip ram_chip_1 (
    .Clear_RAM(Reset_RAM_out), .Write(cpu_24bit_1_ram_write), .Read(cpu_24bit_1_ram_read),
    .Data_Input(cpu_24bit_1_cpu_bus_output), .Load_Address(cpu_24bit_1_load_ram_address),
    .Reset(Reset_System_out), .Enable_Output(cpu_24bit_1_ram_output_enabled), .Clock(cpu_24bit_1_cpu_clock),
    .Data_Output(cpu_24bit_1_cpu_bus_output));
  assign or_1_out = 2'b01 | cpu_24bit_1_ep1;  // OR_Gate or_1, 2 bits wide
  Register_24Bit register_24bit_1 (
    .Load_Store(cpu_24bit_1_ep0), .Input_Data(cpu_24bit_1_cpu_bus_output), .Clock(cpu_24bit_1_cpu_clock),
    .Clear(Reset_System_out), .Output_Display(register_24bit_1_output_display),
    .Output_Data(cpu_24bit_1_cpu_bus_output));
  Register_24Bit register_24bit_2 (
    .Load_Store(or_1_out), .Input_Data({{16{1'b0}}, joystick_1_x}), .Clock(cpu_24bit_1_cpu_clock),
    .Clear(Reset_System_out), .Output_Data(cpu_24bit_1_cpu_bus_output));  // open: Output_Display
  Joystick joystick_1 (.x(joystick_1_x[3:0]), .y(joystick_1_x[7:4]));
  DipSwitch #(.number(1)) Dec_Hex (.sw1(Dec_Hex_sw1));
  Hex_Digit_Display hex_digit_display_1 (.value(valuedisplay_1_o8));  // open: dp
  Hex_Digit_Display hex_digit_display_2 (.value(valuedisplay_1_o7));  // open: dp
  Hex_Digit_Display hex_digit_display_3 (.value(valuedisplay_1_o6));  // open: dp
  Hex_Digit_Display hex_digit_display_4 (.value(valuedisplay_1_o5));  // open: dp
  Hex_Digit_Display hex_digit_display_5 (.value(valuedisplay_1_o4));  // open: dp
  Hex_Digit_Display hex_digit_display_6 (.value(valuedisplay_1_o3));  // open: dp
  Hex_Digit_Display hex_digit_display_7 (.value(valuedisplay_1_o2));  // open: dp
  ValueDisplay valuedisplay_1 (
    .Data(register_24bit_1_output_display), .Clear(Reset_System_out), .Format(Dec_Hex_sw1),
    .O7(valuedisplay_1_o7), .O8(valuedisplay_1_o8), .O1(valuedisplay_1_o1), .O2(valuedisplay_1_o2),
    .O3(valuedisplay_1_o3), .O4(valuedisplay_1_o4), .O5(valuedisplay_1_o5), .O6(valuedisplay_1_o6));
  Hex_Digit_Display hex_digit_display_8 (.value(valuedisplay_1_o1));  // open: dp
endmodule

module CPU_24Bit (
  input  Reset_System,
  input  [23:0] CPU_Bus_Input,
  output [23:0] CPU_Bus_Output,
  output Load_RAM_Address,
  output RAM_Read,
  output RAM_Write,
  output RAM_Output_Enabled,
  output [1:0] EP0,
  output [1:0] EP1,
  output [1:0] EP2,
  output [1:0] EP3,
  output [1:0] EP4,
  output [1:0] EP5,
  output [1:0] EP6,
  output [1:0] EP7,
  output [1:0] EP8,
  output [1:0] EP9,
  output [1:0] EPA,
  output [1:0] EPB,
  output [1:0] EPC,
  output [1:0] EPD,
  output Raw_CPU_Clock,
  output CPU_Clock,
  output [1:0] EPE,
  output [1:0] EPF
);

  wire alu_24bit_1_flag_carry, alu_24bit_1_flag_zero, cpu_firmwarechip_1_decrement_sp,
       cpu_firmwarechip_1_enable_source, cpu_firmwarechip_1_enable_sp, cpu_firmwarechip_1_halt,
       cpu_firmwarechip_1_pc_enable, cpu_firmwarechip_1_register_load, cpu_firmwarechip_1_register_store,
       register_decoder_1_enable_source_expansion_register, register_decoder_1_enable_source_register,
       register_decoder_1_load_expansion_register, register_decoder_1_load_register,
       register_decoder_1_store_expansion_register, register_decoder_1_store_register;
  wire [1:0] alu_24bit_1_flag_compare, register_mapper_1_acc, register_mapper_1_pc, register_mapper_1_rea,
       register_mapper_1_reb, register_mapper_1_rep, register_mapper_1_req, register_mapper_1_rer,
       register_mapper_1_res, register_mapper_1_ret, register_mapper_1_reu, register_mapper_1_rev,
       register_mapper_1_rew, register_mapper_1_rex, register_mapper_1_rey, register_mapper_1_rez,
       register_mapper_1_sp;
  wire [2:0] cpu_firmwarechip_1_alu_operation;
  wire [3:0] register_decoder_1_destination_expansion_register, register_decoder_1_destination_register,
       register_decoder_1_source_expansion_register, register_decoder_1_source_register;
  wire [4:0] cpu_firmwarechip_1_destination_register, cpu_firmwarechip_1_source_register;
  wire [23:0] alu_24bit_1_acc, register_24bit_7_output_display, register_24bit_8_output_display;

  Clock clock_1 (.out(Raw_CPU_Clock));
  and and_1 (CPU_Clock, ~Reset_System, ~cpu_firmwarechip_1_halt, Raw_CPU_Clock);  // AND_Gate
  CPU_FirmwareChip cpu_firmwarechip_1 (
    .Flag_Compare(alu_24bit_1_flag_compare), .Flag_Zero(alu_24bit_1_flag_zero),
    .Flag_Carry(alu_24bit_1_flag_carry), .Data(CPU_Bus_Input), .in_2(CPU_Clock), .Clear(Reset_System),
    .Register_Load(cpu_firmwarechip_1_register_load), .Register_Store(cpu_firmwarechip_1_register_store),
    .PC_Enable(cpu_firmwarechip_1_pc_enable), .RAM_Address_Load(Load_RAM_Address), .RAM_Read(RAM_Read),
    .RAM_Write(RAM_Write), .Decrement_SP(cpu_firmwarechip_1_decrement_sp),
    .Enable_SP(cpu_firmwarechip_1_enable_sp), .Halt(cpu_firmwarechip_1_halt),
    .ALU_Operation(cpu_firmwarechip_1_alu_operation), .Enable_RAM_Output(RAM_Output_Enabled),
    .Enable_Source(cpu_firmwarechip_1_enable_source), .Source_Register(cpu_firmwarechip_1_source_register),
    .Destination_Register(cpu_firmwarechip_1_destination_register));  // open: out_13, out_14, Instruction_Read
  Register_Decoder register_decoder_1 (
    .Destination_Address(cpu_firmwarechip_1_destination_register), .Store(cpu_firmwarechip_1_register_store),
    .Source_Address(cpu_firmwarechip_1_source_register), .Load(cpu_firmwarechip_1_register_load),
    .Enable_Source(cpu_firmwarechip_1_enable_source),
    .Destination_Expansion_Register(register_decoder_1_destination_expansion_register),
    .Destination_Register(register_decoder_1_destination_register),
    .Store_Expansion_Register(register_decoder_1_store_expansion_register),
    .Store_Register(register_decoder_1_store_register),
    .Source_Expansion_Register(register_decoder_1_source_expansion_register),
    .Source_Register(register_decoder_1_source_register),
    .Load_Expansion_Register(register_decoder_1_load_expansion_register),
    .Load_Register(register_decoder_1_load_register),
    .Enable_Source_Expansion_Register(register_decoder_1_enable_source_expansion_register),
    .Enable_Source_Register(register_decoder_1_enable_source_register));
  StackPointer stackpointer_1 (
    .Decrement(cpu_firmwarechip_1_decrement_sp), .Enable(cpu_firmwarechip_1_enable_sp), .Clear(Reset_System),
    .Load(register_mapper_1_sp), .Clock(CPU_Clock), .Data(CPU_Bus_Input), .Pointer(CPU_Bus_Output));
  ProgramCounter_24Bit programcounter_24bit_1 (
    .Clear(Reset_System), .Load(register_mapper_1_pc), .Enable(cpu_firmwarechip_1_pc_enable),
    .Clock(CPU_Clock), .Data(CPU_Bus_Input), .Pointer(CPU_Bus_Output));
  Register_Mapper register_mapper_1 (
    .Load(register_decoder_1_load_register), .Store(register_decoder_1_store_register),
    .Enable_Source(register_decoder_1_enable_source_register), .Source(register_decoder_1_source_register),
    .Address(register_decoder_1_destination_register), .REP(register_mapper_1_rep),
    .SP(register_mapper_1_sp), .PC(register_mapper_1_pc), .REA(register_mapper_1_rea),
    .REB(register_mapper_1_reb), .ACC(register_mapper_1_acc), .REZ(register_mapper_1_rez),
    .REY(register_mapper_1_rey), .REX(register_mapper_1_rex), .REW(register_mapper_1_rew),
    .REV(register_mapper_1_rev), .REU(register_mapper_1_reu), .RET(register_mapper_1_ret),
    .RES(register_mapper_1_res), .RER(register_mapper_1_rer), .REQ(register_mapper_1_req));
  Register_24Bit register_24bit_1 (
    .Load_Store(register_mapper_1_rez), .Input_Data(CPU_Bus_Input), .Clock(CPU_Clock), .Clear(Reset_System),
    .Output_Data(CPU_Bus_Output));  // open: Output_Display
  Register_24Bit register_24bit_2 (
    .Load_Store(register_mapper_1_rey), .Input_Data(CPU_Bus_Input), .Clock(CPU_Clock), .Clear(Reset_System),
    .Output_Data(CPU_Bus_Output));  // open: Output_Display
  Register_24Bit register_24bit_3 (
    .Load_Store(register_mapper_1_rex), .Input_Data(CPU_Bus_Input), .Clock(CPU_Clock), .Clear(Reset_System),
    .Output_Data(CPU_Bus_Output));  // open: Output_Display
  Register_24Bit register_24bit_4 (
    .Load_Store(register_mapper_1_rew), .Input_Data(CPU_Bus_Input), .Clock(CPU_Clock), .Clear(Reset_System),
    .Output_Data(CPU_Bus_Output));  // open: Output_Display
  Register_24Bit register_24bit_5 (
    .Load_Store(register_mapper_1_rev), .Input_Data(CPU_Bus_Input), .Clock(CPU_Clock), .Clear(Reset_System),
    .Output_Data(CPU_Bus_Output));  // open: Output_Display
  Register_24Bit register_24bit_6 (
    .Load_Store(register_mapper_1_reu), .Input_Data(CPU_Bus_Input), .Clock(CPU_Clock), .Clear(Reset_System),
    .Output_Data(CPU_Bus_Output));  // open: Output_Display
  Register_24Bit register_24bit_7 (
    .Load_Store(register_mapper_1_rea), .Input_Data(CPU_Bus_Input), .Clock(CPU_Clock), .Clear(Reset_System),
    .Output_Display(register_24bit_7_output_display), .Output_Data(CPU_Bus_Output));
  Register_24Bit register_24bit_8 (
    .Load_Store(register_mapper_1_reb), .Input_Data(CPU_Bus_Input), .Clock(CPU_Clock), .Clear(Reset_System),
    .Output_Display(register_24bit_8_output_display), .Output_Data(CPU_Bus_Output));
  Expansion_Mapper expansion_mapper_1 (
    .Load(register_decoder_1_load_expansion_register), .Store(register_decoder_1_store_expansion_register),
    .Enable_Source(register_decoder_1_enable_source_expansion_register),
    .Source(register_decoder_1_source_expansion_register),
    .Address(register_decoder_1_destination_expansion_register), .EPD(EPD), .EPE(EPE), .EPF(EPF), .EP0(EP0),
    .EP1(EP1), .EP2(EP2), .EP3(EP3), .EP4(EP4), .EP5(EP5), .EP6(EP6), .EP7(EP7), .EP8(EP8), .EP9(EP9),
    .EPA(EPA), .EPB(EPB), .EPC(EPC));
  Register_24Bit register_24bit_9 (
    .Load_Store(register_mapper_1_ret), .Input_Data(CPU_Bus_Input), .Clock(CPU_Clock), .Clear(Reset_System),
    .Output_Data(CPU_Bus_Output));  // open: Output_Display
  Register_24Bit register_24bit_10 (
    .Load_Store(register_mapper_1_res), .Input_Data(CPU_Bus_Input), .Clock(CPU_Clock), .Clear(Reset_System),
    .Output_Data(CPU_Bus_Output));  // open: Output_Display
  Register_24Bit register_24bit_11 (
    .Load_Store(register_mapper_1_rer), .Input_Data(CPU_Bus_Input), .Clock(CPU_Clock), .Clear(Reset_System),
    .Output_Data(CPU_Bus_Output));  // open: Output_Display
  Register_24Bit register_24bit_12 (
    .Load_Store(register_mapper_1_req), .Input_Data(CPU_Bus_Input), .Clock(CPU_Clock), .Clear(Reset_System),
    .Output_Data(CPU_Bus_Output));  // open: Output_Display
  Register_24Bit register_24bit_13 (
    .Load_Store(register_mapper_1_rep), .Input_Data(CPU_Bus_Input), .Clock(CPU_Clock), .Clear(Reset_System),
    .Output_Data(CPU_Bus_Output));  // open: Output_Display
  ALU_24Bit alu_24bit_1 (
    .SelectMode(cpu_firmwarechip_1_alu_operation), .A(register_24bit_7_output_display),
    .B(register_24bit_8_output_display), .Flag_Carry(alu_24bit_1_flag_carry),
    .Flag_Zero(alu_24bit_1_flag_zero), .ACC(alu_24bit_1_acc), .Flag_Compare(alu_24bit_1_flag_compare));
  Register_24Bit register_24bit_14 (
    .Load_Store(register_mapper_1_acc), .Input_Data(alu_24bit_1_acc), .Clock(CPU_Clock),
    .Clear(Reset_System), .Output_Data(CPU_Bus_Output));  // open: Output_Display

  // Notes on the sheet:
  //   Z
  //   Y
  //   X
  //   W
  //   V
  //   U
  //   A
  //   B
  //   T
  //   S
  //   R
  //   Q
  //   P
  //   ACC
  //   When drawing an image/ pixel to display:
  //   5. CPU takes over again
  //   1. CPU moves set-pixel instruction into this Expansion Register
  //   3. The Display Processor (GPU) now takes over the execution time and proccesses the given instruction
  //   4. The Display sends "finished" instruction into this expansion register once it is done 
  //   2. CPU yields until it reads a "finished" instruction from this Expansion Register (Or a variable look-up instruction for example)
endmodule

module Register_24Bit (
  input  [23:0] Input_Data,
  input  [1:0] Load_Store,
  input  Clock,
  input  Clear,
  output [23:0] Output_Display,
  output [23:0] Output_Data
);

  Register #(.width(24)) register_1 (.D(Input_Data), .en(Load_Store[0]), .clk(Clock), .Q(Output_Display), .clr(Clear));
  assign Output_Data = Load_Store[1] ? Output_Display : 24'bz;  // Controlled_Buffer controlled_buffer_1
endmodule

module ALU_24Bit (
  input  [23:0] A,
  input  [23:0] B,
  input  [2:0] SelectMode,
  output Flag_Carry,
  output Flag_Zero,
  output [1:0] Flag_Compare,
  output [23:0] ACC
);

  wire adder_1_cout, or_24bit_1_data_out, subtractor_1_bout;
  wire [23:0] adder_1_out, and_1_out, divider_1_out, divider_1_rem, multiplier_1_cout, multiplier_1_out,
       or_1_out, or_2_out, shifter_1_out, subtractor_1_out, xor_1_out;

  Adder #(.width(24)) adder_1 (.a(A), .b(B), .out(adder_1_out), .cout(adder_1_cout));  // open: cin
  Subtractor #(.width(24)) subtractor_1 (.a(A), .b(B), .out(subtractor_1_out), .bout(subtractor_1_bout));  // open: bin
  Multiplier #(.width(24)) multiplier_1 (.a(A), .b(B), .out(multiplier_1_out), .cout(multiplier_1_cout));  // open: cin
  Divider #(.width(24)) divider_1 (.a(A), .b(B), .out(divider_1_out), .rem(divider_1_rem));  // open: upper
  Shifter #(.width(24)) shifter_1 (.in(A), .\dist (B[4:0]), .out(shifter_1_out));
  assign and_1_out = A & B;  // AND_Gate and_1, 24 bits wide
  assign or_1_out = A | B;  // OR_Gate or_1, 24 bits wide
  assign xor_1_out = A ^ B;  // XOR_Gate xor_1, 24 bits wide
  Comparator #(.width(24)) comparator_1 (.a(A), .b(B), .gt(Flag_Compare[0]), .lt(Flag_Compare[1]));  // open: eq
  Or_24Bit or_24bit_1 (.Data_In(or_2_out), .Data_Out(or_24bit_1_data_out));
  assign or_2_out = multiplier_1_cout | divider_1_rem;  // OR_Gate or_2, 24 bits wide
  or or_3 (Flag_Carry, adder_1_cout, subtractor_1_bout, or_24bit_1_data_out);
  Comparator #(.width(24)) comparator_2 (.a(subtractor_1_out), .b({24{1'b0}}), .eq(Flag_Zero));  // open: gt, lt
  Multiplexer #(.select(3), .width(24)) multiplexer_1 (
    .in0(adder_1_out), .in1(subtractor_1_out), .in2(multiplier_1_out), .in3(divider_1_out),
    .in4(shifter_1_out), .in5(and_1_out), .in6(or_1_out), .in7(xor_1_out), .out(ACC), .sel(SelectMode));
endmodule

module CPU_FirmwareChip (
  input  [23:0] Data,
  input  in_2,
  input  Clear,
  input  [1:0] Flag_Compare,
  input  Flag_Zero,
  input  Flag_Carry,
  output [4:0] Source_Register,
  output [4:0] Destination_Register,
  output PC_Enable,
  output RAM_Address_Load,
  output RAM_Read,
  output RAM_Write,
  output out_13,
  output out_14,
  output Decrement_SP,
  output Enable_SP,
  output Halt,
  output Instruction_Read,
  output [2:0] ALU_Operation,
  output Enable_RAM_Output,
  output Enable_Source,
  output Register_Load,
  output Register_Store
);

  wire demultiplexer_1_out0, demultiplexer_1_out1, not_1_out, or_1_out, or_2_out;
  wire [3:0] counter_1_q;
  wire [21:0] rom_1_data;
  wire [23:0] register_24bit_1_output_data;

  or or_1 (or_1_out, Clear, Instruction_Read);
  Counter #(.max('hf), .width(4)) counter_1 (
    .clr(or_1_out), .up(1'b1), .count(1'b1), .clk(not_1_out), .Q(counter_1_q));  // open: load, D, carry
  not not_1 (not_1_out, in_2);
  Register_24Bit register_24bit_1 (
    .Load_Store({1'b1, rom_1_data[0]}), .Input_Data(Data), .Clock(in_2), .Clear(Clear),
    .Output_Data(register_24bit_1_output_data));  // open: Output_Display
  Multiplexer #(.width(5)) multiplexer_1 (
    .in0(register_24bit_1_output_data[12:8]), .in1(rom_1_data[21:17]), .out(Source_Register),
    .sel(demultiplexer_1_out0));
  Multiplexer #(.width(5)) multiplexer_2 (
    .in0(register_24bit_1_output_data[17:13]), .in1(rom_1_data[21:17]), .out(Destination_Register),
    .sel(demultiplexer_1_out1));
  ROM #(.addrWidth(24), .dataWidth(24)) rom_1 (
    .addr({Flag_Carry, Flag_Zero, Flag_Compare, {8{1'b0}}, register_24bit_1_output_data[7:0], counter_1_q}),
    .data({Register_Store, Register_Load, rom_1_data[21:17], Enable_Source, Enable_RAM_Output, ALU_Operation, Instruction_Read, Halt, rom_1_data[9], Enable_SP, Decrement_SP, out_14, out_13, RAM_Write, RAM_Read, RAM_Address_Load, PC_Enable, rom_1_data[0]}));
  Demultiplexer demultiplexer_1 (
    .out0(demultiplexer_1_out0), .out1(demultiplexer_1_out1), .in(or_2_out), .sel(rom_1_data[9]));
  or or_2 (or_2_out, rom_1_data[17], rom_1_data[18], rom_1_data[19], rom_1_data[20], rom_1_data[21]);

  // Notes on the sheet:
  //   0-7 opcode
  //   8-11 src register
  //   12-15 dest register
  //   contents of rom_1 (hex, n*v repeats v):
  //   1f0004 800b 800 13*0 1f0004 800b 400 800 12*0 1f0004 800b 810000 800 12*0 1f0004 800b 1f0004 80800a
  //   800 11*0 1f0004 800b 1f0004 800e 808008 800 10*0 1f0004 800b 1f0004 800e 10010 800 10*0 1f0004 800b
  //   10004 400010 800 11*0 1f0004 800b 840200 800 12*0 1f0004 800b 841200 800 12*0 1f0004 800b 842200 800
  //   12*0 1f0004 800b 843200 800 12*0 1f0004 800b 844200 800 12*0 1f0004 800b 845200 800 12*0 1f0004 800b
  //   846200 800 12*0 1f0004 800b 847200 800 12*0 1f0004 800b 1f0004 9e8208 800 11*0 1f0004 800b 410000
  //   800 12*0 1f0004 800b 2 800 12*0 1f0004 800b 2 800 12*0 1f0004 800b 2 800 12*0 1f0004 800b 2 800 12*0
  //   1f0004 800b 1f0004 1d0004 1f0110 1f0004 9e8208 800 8*0 1f0004 800b 1d0004 1f0110 410000 800 10*0
  //   1f0004 800b 180 1d0004 9e8208 2 1f0004 800 8*0 1f0004 800b 10004 808008 800 1048187*0 1f0004 800b
  //   800 13*0 1f0004 800b 400 800 12*0 1f0004 800b 810000 800 12*0 1f0004 800b 1f0004 80800a 800 11*0
  //   1f0004 800b 1f0004 800e 808008 800 10*0 1f0004 800b 1f0004 800e 10010 800 10*0 1f0004 800b 10004
  //   400010 800 11*0 1f0004 800b 840200 800 12*0 1f0004 800b 841200 800 12*0 1f0004 800b 842200 800 12*0
  //   1f0004 800b 843200 800 12*0 1f0004 800b 844200 800 12*0 1f0004 800b 845200 800 12*0 1f0004 800b
  //   846200 800 12*0 1f0004 800b 847200 800 12*0 1f0004 800b 1f0004 9e8208 800 11*0 1f0004 800b 410000
  //   800 12*0 1f0004 800b 2 800 12*0 1f0004 800b 2 800 12*0 1f0004 800b 2 800 12*0 1f0004 800b 2 800 12*0
  //   1f0004 800b 1f0004 1d0004 1f0110 1f0004 9e8208 800 8*0 1f0004 800b 1d0004 1f0110 410000 800 10*0
  //   1f0004 800b 180 1d0004 9e8208 2 1f0004 800 8*0 1f0004 800b 10004 808008 800 1048187*0 1f0004 800b
  //   800 13*0 1f0004 800b 400 800 12*0 1f0004 800b 810000 800 12*0 1f0004 800b 1f0004 80800a 800 11*0
  //   1f0004 800b 1f0004 800e 808008 800 10*0 1f0004 800b 1f0004 800e 10010 800 10*0 1f0004 800b 10004
  //   400010 800 11*0 1f0004 800b 840200 800 12*0 1f0004 800b 841200 800 12*0 1f0004 800b 842200 800 12*0
  //   1f0004 800b 843200 800 12*0 1f0004 800b 844200 800 12*0 1f0004 800b 845200 800 12*0 1f0004 800b
  //   846200 800 12*0 1f0004 800b 847200 800 12*0 1f0004 800b 1f0004 9e8208 800 11*0 1f0004 800b 410000
  //   800 12*0 1f0004 800b 2 800 12*0 1f0004 800b 2 800 12*0 1f0004 800b 2 800 12*0 1f0004 800b 2 800 12*0
  //   1f0004 800b 1f0004 1d0004 1f0110 1f0004 9e8208 800 8*0 1f0004 800b 1d0004 1f0110 410000 800 10*0
  //   1f0004 800b 180 1d0004 9e8208 2 1f0004 800 8*0 1f0004 800b 10004 808008 800 1048187*0 1f0004 800b
  //   800 13*0 1f0004 800b 400 800 12*0 1f0004 800b 810000 800 12*0 1f0004 800b 1f0004 80800a 800 11*0
  //   1f0004 800b 1f0004 800e 808008 800 10*0 1f0004 800b 1f0004 800e 10010 800 10*0 1f0004 800b 10004
  //   400010 800 11*0 1f0004 800b 840200 800 12*0 1f0004 800b 841200 800 12*0 1f0004 800b 842200 800 12*0
  //   1f0004 800b 843200 800 12*0 1f0004 800b 844200 800 12*0 1f0004 800b 845200 800 12*0 1f0004 800b
  //   846200 800 12*0 1f0004 800b 847200 800 12*0 1f0004 800b 1f0004 9e8208 800 11*0 1f0004 800b 410000
  //   800 12*0 1f0004 800b 2 800 12*0 1f0004 800b 2 800 12*0 1f0004 800b 2 800 12*0 1f0004 800b 2 800 12*0
  //   1f0004 800b 1f0004 1d0004 1f0110 1f0004 9e8208 800 8*0 1f0004 800b 1d0004 1f0110 410000 800 10*0
  //   1f0004 800b 180 1d0004 9e8208 2 1f0004 800 8*0 1f0004 800b 10004 808008 800 1048187*0 1f0004 800b
  //   800 13*0 1f0004 800b 400 800 12*0 1f0004 800b 810000 800 12*0 1f0004 800b 1f0004 80800a 800 11*0
  //   1f0004 800b 1f0004 800e 808008 800 10*0 1f0004 800b 1f0004 800e 10010 800 10*0 1f0004 800b 10004
  //   400010 800 11*0 1f0004 800b 840200 800 12*0 1f0004 800b 841200 800 12*0 1f0004 800b 842200 800 12*0
  //   1f0004 800b 843200 800 12*0 1f0004 800b 844200 800 12*0 1f0004 800b 845200 800 12*0 1f0004 800b
  //   846200 800 12*0 1f0004 800b 847200 800 12*0 1f0004 800b 1f0004 9e8208 800 11*0 1f0004 800b 410000
  //   800 12*0 1f0004 800b 1f0004 9e8208 800 11*0 1f0004 800b 410000 800 12*0 1f0004 800b 2 800 12*0
  //   1f0004 800b 2 800 12*0 1f0004 800b 1f0004 1d0004 1f0110 1f0004 9e8208 800 8*0 1f0004 800b 1d0004
  //   1f0110 410000 800 10*0 1f0004 800b 180 1d0004 9e8208 2 1f0004 800 8*0 1f0004 800b 10004 808008 800
  //   1048187*0 1f0004 800b 800 13*0 1f0004 800b 400 800 12*0 1f0004 800b 81000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
endmodule

module Or_24Bit (
  input  [23:0] Data_In,
  output Data_Out
);

  or or_1 (Data_Out, Data_In[0], Data_In[1], Data_In[2], Data_In[3], Data_In[4], Data_In[5], Data_In[6], Data_In[7], Data_In[8], Data_In[9], Data_In[10], Data_In[11], Data_In[12], Data_In[13], Data_In[14], Data_In[15], Data_In[16], Data_In[17], Data_In[18], Data_In[19], Data_In[20], Data_In[21], Data_In[22], Data_In[23]);
endmodule

module Register_Mapper (
  input  [3:0] Source,
  input  Enable_Source,
  input  [3:0] Address,
  input  Load,
  input  Store,
  output [1:0] REA,
  output [1:0] REB,
  output [1:0] ACC,
  output [1:0] REZ,
  output [1:0] REY,
  output [1:0] REX,
  output [1:0] REW,
  output [1:0] REV,
  output [1:0] REU,
  output [1:0] RET,
  output [1:0] RES,
  output [1:0] RER,
  output [1:0] REQ,
  output [1:0] REP,
  output [1:0] SP,
  output [1:0] PC
);

  wire [1:0] demultiplexer_1_out0, demultiplexer_1_out1, demultiplexer_1_out2, demultiplexer_1_out3,
       demultiplexer_1_out4, demultiplexer_1_out5, demultiplexer_1_out6, demultiplexer_1_out7,
       demultiplexer_1_out8, demultiplexer_1_out9, demultiplexer_1_out10, demultiplexer_1_out11,
       demultiplexer_1_out12, demultiplexer_1_out13, demultiplexer_1_out14, demultiplexer_1_out15,
       demultiplexer_2_out0, demultiplexer_2_out1, demultiplexer_2_out2, demultiplexer_2_out3,
       demultiplexer_2_out4, demultiplexer_2_out5, demultiplexer_2_out6, demultiplexer_2_out7,
       demultiplexer_2_out8, demultiplexer_2_out9, demultiplexer_2_out10, demultiplexer_2_out11,
       demultiplexer_2_out12, demultiplexer_2_out13, demultiplexer_2_out14, demultiplexer_2_out15,
       multiplexer_1_out;

  Multiplexer #(.width(2)) multiplexer_1 (.in0(2'b00), .in1(2'b10), .out(multiplexer_1_out), .sel(Enable_Source));
  Demultiplexer #(.select(4), .width(2)) demultiplexer_1 (
    .out0(demultiplexer_1_out0), .out1(demultiplexer_1_out1), .out2(demultiplexer_1_out2),
    .out3(demultiplexer_1_out3), .out4(demultiplexer_1_out4), .out5(demultiplexer_1_out5),
    .out6(demultiplexer_1_out6), .out7(demultiplexer_1_out7), .out8(demultiplexer_1_out8),
    .out9(demultiplexer_1_out9), .out10(demultiplexer_1_out10), .out11(demultiplexer_1_out11),
    .out12(demultiplexer_1_out12), .out13(demultiplexer_1_out13), .out14(demultiplexer_1_out14),
    .out15(demultiplexer_1_out15), .in(multiplexer_1_out), .sel(Source));
  Demultiplexer #(.select(4), .width(2)) demultiplexer_2 (
    .out0(demultiplexer_2_out0), .out1(demultiplexer_2_out1), .out2(demultiplexer_2_out2),
    .out3(demultiplexer_2_out3), .out4(demultiplexer_2_out4), .out5(demultiplexer_2_out5),
    .out6(demultiplexer_2_out6), .out7(demultiplexer_2_out7), .out8(demultiplexer_2_out8),
    .out9(demultiplexer_2_out9), .out10(demultiplexer_2_out10), .out11(demultiplexer_2_out11),
    .out12(demultiplexer_2_out12), .out13(demultiplexer_2_out13), .out14(demultiplexer_2_out14),
    .out15(demultiplexer_2_out15), .in({Load, Store}), .sel(Address));
  assign REA = demultiplexer_1_out0 | demultiplexer_2_out0;  // OR_Gate or_1, 2 bits wide
  assign REB = demultiplexer_1_out1 | demultiplexer_2_out1;  // OR_Gate or_2, 2 bits wide
  assign ACC = demultiplexer_1_out2 | demultiplexer_2_out2;  // OR_Gate or_3, 2 bits wide
  assign REZ = demultiplexer_1_out3 | demultiplexer_2_out3;  // OR_Gate or_4, 2 bits wide
  assign REY = demultiplexer_1_out4 | demultiplexer_2_out4;  // OR_Gate or_5, 2 bits wide
  assign REX = demultiplexer_1_out5 | demultiplexer_2_out5;  // OR_Gate or_6, 2 bits wide
  assign REW = demultiplexer_1_out6 | demultiplexer_2_out6;  // OR_Gate or_7, 2 bits wide
  assign REV = demultiplexer_1_out7 | demultiplexer_2_out7;  // OR_Gate or_8, 2 bits wide
  assign REU = demultiplexer_1_out8 | demultiplexer_2_out8;  // OR_Gate or_9, 2 bits wide
  assign RET = demultiplexer_1_out9 | demultiplexer_2_out9;  // OR_Gate or_10, 2 bits wide
  assign RES = demultiplexer_1_out10 | demultiplexer_2_out10;  // OR_Gate or_11, 2 bits wide
  assign RER = demultiplexer_1_out11 | demultiplexer_2_out11;  // OR_Gate or_12, 2 bits wide
  assign REQ = demultiplexer_1_out12 | demultiplexer_2_out12;  // OR_Gate or_13, 2 bits wide
  assign REP = demultiplexer_1_out13 | demultiplexer_2_out13;  // OR_Gate or_14, 2 bits wide
  assign SP = demultiplexer_1_out14 | demultiplexer_2_out14;  // OR_Gate or_15, 2 bits wide
  assign PC = demultiplexer_1_out15 | demultiplexer_2_out15;  // OR_Gate or_16, 2 bits wide
endmodule

module ProgramCounter_24Bit (
  input  Clear,
  input  [1:0] Load,
  input  Enable,
  input  Clock,
  input  [23:0] Data,
  output [23:0] Pointer
);

  wire [23:0] counter_1_q;

  Counter #(.max('hffffff), .width(24)) counter_1 (
    .clr(Clear), .load(Load[0]), .count(Enable), .clk(Clock), .D(Data), .Q(counter_1_q));  // open: up, carry
  assign Pointer = Load[1] ? counter_1_q : 24'bz;  // Controlled_Buffer controlled_buffer_1
endmodule

module Expansion_Mapper (
  input  [3:0] Source,
  input  Enable_Source,
  input  [3:0] Address,
  input  Load,
  input  Store,
  output [1:0] EP0,
  output [1:0] EP1,
  output [1:0] EP2,
  output [1:0] EP3,
  output [1:0] EP4,
  output [1:0] EP5,
  output [1:0] EP6,
  output [1:0] EP7,
  output [1:0] EP8,
  output [1:0] EP9,
  output [1:0] EPA,
  output [1:0] EPB,
  output [1:0] EPC,
  output [1:0] EPD,
  output [1:0] EPE,
  output [1:0] EPF
);

  wire [1:0] demultiplexer_1_out0, demultiplexer_1_out1, demultiplexer_1_out2, demultiplexer_1_out3,
       demultiplexer_1_out4, demultiplexer_1_out5, demultiplexer_1_out6, demultiplexer_1_out7,
       demultiplexer_1_out8, demultiplexer_1_out9, demultiplexer_1_out10, demultiplexer_1_out11,
       demultiplexer_1_out12, demultiplexer_1_out13, demultiplexer_1_out14, demultiplexer_1_out15,
       demultiplexer_2_out0, demultiplexer_2_out1, demultiplexer_2_out2, demultiplexer_2_out3,
       demultiplexer_2_out4, demultiplexer_2_out5, demultiplexer_2_out6, demultiplexer_2_out7,
       demultiplexer_2_out8, demultiplexer_2_out9, demultiplexer_2_out10, demultiplexer_2_out11,
       demultiplexer_2_out12, demultiplexer_2_out13, demultiplexer_2_out14, demultiplexer_2_out15,
       multiplexer_1_out;

  Multiplexer #(.width(2)) multiplexer_1 (.in0(2'b00), .in1(2'b10), .out(multiplexer_1_out), .sel(Enable_Source));
  Demultiplexer #(.select(4), .width(2)) demultiplexer_1 (
    .out0(demultiplexer_1_out0), .out1(demultiplexer_1_out1), .out2(demultiplexer_1_out2),
    .out3(demultiplexer_1_out3), .out4(demultiplexer_1_out4), .out5(demultiplexer_1_out5),
    .out6(demultiplexer_1_out6), .out7(demultiplexer_1_out7), .out8(demultiplexer_1_out8),
    .out9(demultiplexer_1_out9), .out10(demultiplexer_1_out10), .out11(demultiplexer_1_out11),
    .out12(demultiplexer_1_out12), .out13(demultiplexer_1_out13), .out14(demultiplexer_1_out14),
    .out15(demultiplexer_1_out15), .in(multiplexer_1_out), .sel(Source));
  Demultiplexer #(.select(4), .width(2)) demultiplexer_2 (
    .out0(demultiplexer_2_out0), .out1(demultiplexer_2_out1), .out2(demultiplexer_2_out2),
    .out3(demultiplexer_2_out3), .out4(demultiplexer_2_out4), .out5(demultiplexer_2_out5),
    .out6(demultiplexer_2_out6), .out7(demultiplexer_2_out7), .out8(demultiplexer_2_out8),
    .out9(demultiplexer_2_out9), .out10(demultiplexer_2_out10), .out11(demultiplexer_2_out11),
    .out12(demultiplexer_2_out12), .out13(demultiplexer_2_out13), .out14(demultiplexer_2_out14),
    .out15(demultiplexer_2_out15), .in({Load, Store}), .sel(Address));
  assign EP0 = demultiplexer_1_out0 | demultiplexer_2_out0;  // OR_Gate or_1, 2 bits wide
  assign EP1 = demultiplexer_1_out1 | demultiplexer_2_out1;  // OR_Gate or_2, 2 bits wide
  assign EP2 = demultiplexer_1_out2 | demultiplexer_2_out2;  // OR_Gate or_3, 2 bits wide
  assign EP3 = demultiplexer_1_out3 | demultiplexer_2_out3;  // OR_Gate or_4, 2 bits wide
  assign EP4 = demultiplexer_1_out4 | demultiplexer_2_out4;  // OR_Gate or_5, 2 bits wide
  assign EP5 = demultiplexer_1_out5 | demultiplexer_2_out5;  // OR_Gate or_6, 2 bits wide
  assign EP6 = demultiplexer_1_out6 | demultiplexer_2_out6;  // OR_Gate or_7, 2 bits wide
  assign EP7 = demultiplexer_1_out7 | demultiplexer_2_out7;  // OR_Gate or_8, 2 bits wide
  assign EP8 = demultiplexer_1_out8 | demultiplexer_2_out8;  // OR_Gate or_9, 2 bits wide
  assign EP9 = demultiplexer_1_out9 | demultiplexer_2_out9;  // OR_Gate or_10, 2 bits wide
  assign EPA = demultiplexer_1_out10 | demultiplexer_2_out10;  // OR_Gate or_11, 2 bits wide
  assign EPB = demultiplexer_1_out11 | demultiplexer_2_out11;  // OR_Gate or_12, 2 bits wide
  assign EPC = demultiplexer_1_out12 | demultiplexer_2_out12;  // OR_Gate or_13, 2 bits wide
  assign EPD = demultiplexer_1_out13 | demultiplexer_2_out13;  // OR_Gate or_14, 2 bits wide
  assign EPE = demultiplexer_1_out14 | demultiplexer_2_out14;  // OR_Gate or_15, 2 bits wide
  assign EPF = demultiplexer_1_out15 | demultiplexer_2_out15;  // OR_Gate or_16, 2 bits wide
endmodule

module RAM_Chip (
  input  Clear_RAM,
  input  Write,
  input  Read,
  input  [23:0] Data_Input,
  input  Load_Address,
  input  Clock,
  input  Reset,
  input  Enable_Output,
  output [23:0] Data_Output
);

  wire [23:0] ram_1_dout, register_24bit_1_output_data;

  Register_24Bit register_24bit_1 (
    .Load_Store({1'b1, Load_Address}), .Input_Data(Data_Input), .Clock(Clock), .Clear(Reset),
    .Output_Data(register_24bit_1_output_data));  // open: Output_Display
  RAM #(.addrWidth(24), .clearpin("true"), .dataWidth(24), .trigger("high"), .\type ("nonvolatile")) ram_1 (
    .addr(register_24bit_1_output_data), .we(Write), .oe(Read), .din(Data_Input), .dout(ram_1_dout),
    .clr(Clear_RAM));
  assign Data_Output = Enable_Output ? ram_1_dout : 24'bz;  // Controlled_Buffer controlled_buffer_1
endmodule

module Register_Decoder (
  input  [4:0] Destination_Address,
  input  Store,
  input  [4:0] Source_Address,
  input  Load,
  input  Enable_Source,
  output [3:0] Destination_Expansion_Register,
  output [3:0] Destination_Register,
  output Store_Expansion_Register,
  output Store_Register,
  output [3:0] Source_Expansion_Register,
  output [3:0] Source_Register,
  output Load_Expansion_Register,
  output Load_Register,
  output Enable_Source_Expansion_Register,
  output Enable_Source_Register
);

  wire not_1_out, not_2_out;

  not not_1 (not_1_out, Destination_Address[4]);
  not not_2 (not_2_out, Source_Address[4]);
  Demultiplexer #(.width(4)) demultiplexer_1 (
    .out0(Destination_Expansion_Register), .out1(Destination_Register), .in(Destination_Address[3:0]),
    .sel(not_1_out));
  Demultiplexer demultiplexer_2 (.out0(Store_Expansion_Register), .out1(Store_Register), .in(Store), .sel(not_1_out));
  Demultiplexer #(.width(4)) demultiplexer_3 (
    .out0(Source_Expansion_Register), .out1(Source_Register), .in(Source_Address[3:0]), .sel(not_2_out));
  Demultiplexer demultiplexer_4 (.out0(Load_Expansion_Register), .out1(Load_Register), .in(Load), .sel(not_2_out));
  Demultiplexer demultiplexer_5 (
    .out0(Enable_Source_Expansion_Register), .out1(Enable_Source_Register), .in(Enable_Source),
    .sel(not_2_out));
endmodule

module ValueDisplay (
  input  [23:0] Data,
  input  Clear,
  input  Format,
  output [3:0] O1,
  output [3:0] O2,
  output [3:0] O3,
  output [3:0] O4,
  output [3:0] O5,
  output [3:0] O6,
  output [3:0] O7,
  output [3:0] O8
);

  wire clock_1_out;
  wire [19:0] undriven, undriven_2, undriven_3, undriven_4, undriven_5, undriven_6, undriven_7, undriven_8;
  wire [23:4] register_24bit_1_output_display, register_24bit_2_output_display,
       register_24bit_3_output_display, register_24bit_4_output_display, register_24bit_5_output_display,
       register_24bit_6_output_display, register_24bit_7_output_display, register_24bit_8_output_display;

  Clock clock_1 (.out(clock_1_out));
  Register_24Bit register_24bit_1 (
    .Load_Store(2'b01), .Input_Data({undriven, Data[3:0]}), .Clock(clock_1_out), .Clear(Clear),
    .Output_Display({register_24bit_1_output_display, O1}));  // open: Output_Data
  Register_24Bit register_24bit_2 (
    .Load_Store(2'b01), .Input_Data({undriven_2, Data[7:4]}), .Clock(clock_1_out), .Clear(Clear),
    .Output_Display({register_24bit_2_output_display, O2}));  // open: Output_Data
  Register_24Bit register_24bit_3 (
    .Load_Store(2'b01), .Input_Data({undriven_3, Data[11:8]}), .Clock(clock_1_out), .Clear(Clear),
    .Output_Display({register_24bit_3_output_display, O3}));  // open: Output_Data
  Register_24Bit register_24bit_4 (
    .Load_Store(2'b01), .Input_Data({undriven_4, Data[15:12]}), .Clock(clock_1_out), .Clear(Clear),
    .Output_Display({register_24bit_4_output_display, O4}));  // open: Output_Data
  Register_24Bit register_24bit_5 (
    .Load_Store(2'b01), .Input_Data({undriven_5, Data[19:16]}), .Clock(clock_1_out), .Clear(Clear),
    .Output_Display({register_24bit_5_output_display, O5}));  // open: Output_Data
  Register_24Bit register_24bit_6 (
    .Load_Store(2'b01), .Input_Data({undriven_6, Data[23:20]}), .Clock(clock_1_out), .Clear(Clear),
    .Output_Display({register_24bit_6_output_display, O6}));  // open: Output_Data
  Register_24Bit register_24bit_7 (
    .Load_Store(2'b01), .Input_Data({undriven_7, 4'b0000}), .Clock(clock_1_out), .Clear(Clear),
    .Output_Display({register_24bit_7_output_display, O7}));  // open: Output_Data
  Register_24Bit register_24bit_8 (
    .Load_Store(2'b01), .Input_Data({undriven_8, 4'b0000}), .Clock(clock_1_out), .Clear(Clear),
    .Output_Display({register_24bit_8_output_display, O8}));  // open: Output_Data

  // Notes on the sheet:
  //   Still need to add a way to display the value as decimal
  //   24Bit Register is overkill, but I didnt want to just create a new 4 bit register just for this
endmodule

module StackPointer (
  input  Clear,
  input  [1:0] Load,
  input  Decrement,
  input  Enable,
  input  Clock,
  input  [23:0] Data,
  output [23:0] Pointer
);

  wire [23:0] counter_1_q;

  Counter #(.max('hffffff), .width(24)) counter_1 (
    .clr(Clear), .load(Load[0]), .up(Decrement), .count(Enable), .clk(Clock), .D(Data), .Q(counter_1_q));  // open: carry
  assign Pointer = Load[1] ? counter_1_q : 24'bz;  // Controlled_Buffer controlled_buffer_1
endmodule

module InputRegister (
  input  in_1
);

  Register #(.width(24)) register_1 ();  // open: D, en, clk, Q, clr
endmodule
